# Fritzing sketch ESP8266 JIG (saved by Fritzing 0.9.3b)
breadboards: 2

parts:
  Prog = Pushbutton [package="[THT]"]
  OLED = Module display OLED I2C 128x64 SSD1306 [package=THT]
  U2 = ESP8266 WiFi Module [part_number=ESP8266]
  Composant3 = FTDI Basic Programmer
  U3 = ESP8266 WiFi Module [part_number=ESP8266]
  R2 = Resistor [tolerance=±5% resistance=10k package=THT]
  R1 = Resistor [tolerance=±5% resistance=10k package=THT]
  R3 = Resistor [tolerance=±5% resistance=10k package=THT]
  S1 = Toggle Switch [package=THT]
  C1 = Electrolytic Capacitor [capacitance=10µF voltage=10V package="100 mil [THT, electrolytic]"]
  R4 = Resistor [tolerance=±5% resistance=10k package=THT]
  Reset = Pushbutton [package="[THT]"]
  C3 = Electrolytic Capacitor [capacitance=100µF voltage=10V package="100 mil [THT, electrolytic]"]
  J2 = female pin header, 4 pins [form="♀ (female)"]
  J9 = female pin header, 11 pins [form="♀ (female)"]
  J8 = female pin header, 11 pins [form="♀ (female)"]
  S2 = Toggle Switch [package=THT]
  S4 = Toggle Switch [package=THT]
  S3 = Toggle Switch [package=THT]
  Composant5 = Arduino Nano (Rev3.0)
  J5 = female pin header, 1 pin [form="♀ (female)"]
  J4 = female pin header, 1 pin [form="♀ (female)"]
  LED = LED - 3mm [color="Red (633nm)" package="3 mm [THT]"]
  R5 = Resistor [tolerance=±5% resistance=470 package=THT]
  Temp = Temperature sensor [package="TO92 [THT]"]
  Pot = Rotary Potentiometer (Small) [maximum_resistance=100kΩ package=THT]
  J7 = female pin header, 1 pin [form="♀ (female)"]
  J6 = female pin header, 1 pin [form="♀ (female)"]
  R6 = Resistor [tolerance=±5% resistance=4.7k package=THT]
  LED1 = LED - 3mm [color="Red (633nm)" package="3 mm [THT]"]
  R7 = Resistor [tolerance=±5% resistance=470 package=THT]
  R8 = Trimmer Potentiometer [maximum_resistance=10kΩ package=THT]
  R9 = Resistor [tolerance=±5% resistance=10k package=THT]
  S5 = Toggle Switch [package=THT]
  R10 = Resistor [tolerance=±1% resistance=20k package=THT]
  J10 = female pin header, 2 pins [form="♀ (female)"]

nets:
  GND: Prog.Pin_1, Prog.Pin_2, OLED.GND, U2.GND, Composant3.GND, U3.GND#12, U3.IO15, Reset.Pin_1, Reset.Pin_2, C3.-, J2.pin4, J8.pin1, J8.pin11, Composant5.GND, R5.Pin_1, Temp.GND, Pot.leg2, R7.Pin_0, R8.leg1, R10.Pin_1
  N1: Prog.Pin_3, Prog.Pin_4, R3.Pin_1, S1.L2
  3.3V: OLED.VCC, U2.VCC, U3.3.3V#11, R2.Pin_1, R1.Pin_1, R3.Pin_0, R4.Pin_0, C3.+, J2.pin3, J9.pin1, Temp.Vdd, Pot.leg1, R6.Pin_0
  N2: OLED.SCL, J2.pin2, S4.L1
  N3: OLED.SDA, J2.pin1, S2.L1
  N4: U2.RXD, U3.RX, S5.COM
  N5: U2.GPIO_0, U3.IO0, S1.COM, J9.pin11
  N6: U2.RST, U3.RST, R2.Pin_0, C1.+, J8.pin5
  N7: U2.GPIO_2, S4.COM
  N8: U2.CH_PD, U3.CHIP_EN, R1.Pin_0, J8.pin6
  N9: U2.TXD, Composant3.RXI, U3.TX, Composant5.D4, J10.pin2
  N10: Composant3.TXO, S5.L1
  N11: U3.IO2, J9.pin10
  N12: U3.D2, J9.pin9
  N13: U3.CLK, J9.pin8
  N14: U3.CMD, J9.pin7
  N15: U3.D0, J9.pin6
  N16: U3.D1, J9.pin5
  N17: U3.D3, J9.pin4
  N18: U3.IO4, J9.pin3
  N19: U3.3.3V#10, J9.pin2
  N20: U3.GND#13, J8.pin2
  N21: U3.IO5, J8.pin3
  N22: U3.T_OUT, J8.pin4
  N23: U3.XPD, J8.pin7
  N24: U3.IO14, J8.pin8
  N25: U3.IO12, J8.pin9
  N26: U3.IO13, J8.pin10
  N27: S1.L1, S2.COM
  N28: C1.-, R4.Pin_1, Reset.Pin_3, Reset.Pin_4
  N29: S2.L2, S3.COM, J4.pin1
  N30: S4.L2, J5.pin1, Temp.DQ, R6.Pin_1
  N31: S3.L1, LED.anode, J6.pin1
  N32: S3.L2, Pot.wiper, J7.pin1
  N33: Composant5.D3, R9.Pin_1, J10.pin1
  N34: Composant5.D7, LED1.anode
  N35: Composant5.5V, R8.leg2
  N36: Composant5.A0, R8.wiper
  N37: LED.cathode, R5.Pin_0
  N38: LED1.cathode, R7.Pin_1
  N39: R9.Pin_0, S5.L2, R10.Pin_0

notes:
  +5V
  +3.3V
  Pro
  Ext
  Ole
  Test
  LED
  Pot
  Rx/D4
  Tx/D3
  USB
  5V

custom parts:
  Module display OLED I2C 128x64 SSD1306: Ecran OLED I2C SSD163 de 128x64 avec connexion I2C
  ESP8266 WiFi Module: Generic WiFi Module based on the ESP8266 with onboard PCB antenna and UART communications
  Temperature sensor: Dellas temperature sensor
